# Fritzing sketch ISA team's scheme (saved by Fritzing 1.0.6)

parts:
  M1 = gear-motor
  M2 = gear-motor
  M3 = gear-motor
  M4 = gear-motor
  A1 = esp32-devkit-38p-expansion-board_1
  A2 = motor-driver-ZK-5AD_1
  A3 = motor-driver-ZK-5AD_1
  U1 = ESP32-38PinWide [part_number=ESP32-38PinWide]
  J1 = Camdenboss_CTB0158-8_5_08mm_pitch [part_number="wago_ 250-202"]
  J2 = Camdenboss_CTB0158-8_5_08mm_pitch [part_number="wago_ 250-202"]
  J3 = Camdenboss_CTB0158-8_5_08mm_pitch [part_number="wago_ 250-202"]
  J4 = Camdenboss_CTB0158-8_5_08mm_pitch [part_number="wago_ 250-202"]
  J5 = Camdenboss_CTB0158-8_5_08mm_pitch [part_number="wago_ 250-202"]
  VCC1 = Battery [internal_resistance=0.1Ω]  # not connected

nets:
  N1: M1.pin_1, A3.connector10
  N2: M1.pin_2, A3.connector9
  N3: M2.pin_1, A2.connector8
  N4: M2.pin_2, A2.connector7
  N5: M3.pin_1, A3.connector8
  N6: M3.pin_2, A3.connector7
  N7: M4.pin_1, A2.connector10
  N8: M4.pin_2, A2.connector9
  N9: A1.connector4, A3.connector5
  N10: A1.connector5, A3.connector4
  N11: A1.connector6, A3.connector3
  N12: A1.connector7, A3.connector2
  N13: A1.connector9, A2.connector5
  N14: A1.connector10, A2.connector4
  N15: A1.connector11, A2.connector3
  N16: A1.connector12, A2.connector2
  N17: A1.connector43, A3.connector0
  N18: A1.connector47, A2.connector0
  N19: A1.connector78, U1.connector0
  N20: A1.connector79, U1.connector1
  N21: A1.connector80, U1.connector2
  N22: A1.connector81, U1.connector3
  N23: A1.connector82, U1.connector4
  N24: A1.connector83, U1.connector5
  N25: A1.connector84, U1.connector6
  N26: A1.connector85, U1.connector7
  N27: A1.connector86, U1.connector8
  N28: A1.connector87, U1.connector9
  N29: A1.connector88, U1.connector10
  N30: A1.connector89, U1.connector11
  N31: A1.connector90, U1.connector12
  N32: A1.connector91, U1.connector13
  N33: A1.connector92, U1.connector14
  N34: A1.connector93, U1.connector15
  N35: A1.connector94, U1.connector16
  N36: A1.connector95, U1.connector17
  N37: A1.connector96, U1.connector18
  N38: A1.connector100, U1.connector19
  N39: A1.connector101, U1.connector20
  N40: A1.connector102, U1.connector21
  N41: A1.connector103, U1.connector22
  N42: A1.connector104, U1.connector23
  N43: A1.connector105, U1.connector24
  N44: A1.connector106, U1.connector25
  N45: A1.connector107, U1.connector26
  N46: A1.connector108, U1.connector27
  N47: A1.connector109, U1.connector28
  N48: A1.connector110, U1.connector29
  N49: A1.connector111, U1.connector30
  N50: A1.connector112, U1.connector31
  N51: A1.connector113, U1.connector32
  N52: A1.connector114, U1.connector33
  N53: A1.connector115, U1.connector34
  N54: A1.connector116, U1.connector35
  N55: A1.connector117, U1.connector36
  N56: A1.connector118, U1.connector37
  N57: A2.connector11, J1.connector1
  N58: A2.connector12, J2.connector1
  N59: A3.connector11, J1.connector0
  N60: A3.connector12, J2.connector0
  N61: J3.connector0, J4.connector1
  N62: J3.connector1, J5.connector1
